// Digital circuit ALU.dig as structural Verilog
module ALU (
  input  [2:0] ctrl,
  input  [31:0] s1,
  input  [31:0] s2,
  output [31:0] result
);

  wire [31:0] add_1_s;

  Add #(.Bits(32)) add_1 (.a(s1), .b(s2), .c_i(1'b0), .s(add_1_s));  // open: c_o
  Multiplexer #(.Selector_Bits(3), .Bits(32)) multiplexer_1 (
    .sel(ctrl), .in_0(add_1_s), .in_1({32{1'b0}}), .in_2({32{1'b0}}), .in_3({32{1'b0}}), .in_4({32{1'b0}}),
    .in_5({32{1'b0}}), .in_6({32{1'b0}}), .in_7({32{1'b0}}), .out(result));
endmodule
