// Digital circuit AddressDecorder.dig as structural Verilog
module AddressDecorder (
  input  [31:0] A,
  input  [31:0] WD,
  output GPUen,
  output [23:0] A_share,
  output [31:0] D,
  output GCen,
  output RAMen
);

  and and_1 (RAMen, ~A[24], ~A[25], ~A[26], ~A[27], ~A[28], ~A[29], ~A[30], ~A[31]);  // And
  and and_2 (GPUen, ~A[24], A[25], ~A[26], ~A[27], ~A[28], ~A[29], ~A[30], ~A[31]);  // And
  and and_3 (GCen, A[24], ~A[25], ~A[26], ~A[27], ~A[28], ~A[29], ~A[30], ~A[31]);  // And

  assign A_share = A[23:0];
  assign D = WD;

  // Other names for the same wires on the sheet: share[23:0] = A[23:0]; Adec_0 = A[24]; Adec_1 = A[25];
  //   Adec_2 = A[26]; Adec_3 = A[27]; Adec_4 = A[28]; Adec_5 = A[29]; Adec_6 = A[30]; Adec_7 = A[31]
endmodule
