// Digital circuit Extender.dig as structural Verilog
module Extender (
  input  [1:0] Immsrc,
  input  [24:0] imm,
  output [31:0] extend
);

  Multiplexer #(.Bits(32), .Selector_Bits(2)) multiplexer_1 (
    .sel(Immsrc), .in_0({{20{1'b0}}, imm[24:13]}), .in_1({32{1'b0}}), .in_2({32{1'b0}}), .in_3({32{1'b0}}),
    .out(extend));
endmodule
