// Digital circuit GameControllerIO.dig as structural Verilog
module GameControllerIO (
  input  [31:0] _1P,
  input  [31:0] _2P,
  input  [31:0] _3P,
  input  [31:0] _4P,
  input  C,
  input  WE,
  input  [23:0] A,
  input  [31:0] Din,
  input  en,
  output [31:0] D
);

  wire and_1_out, demultiplexer_1_out_0, demultiplexer_1_out_1, demultiplexer_1_out_2, demultiplexer_1_out_3;
  wire [31:0] d_ff_1_q, d_ff_2_q, d_ff_3_q, d_ff_4_q, multiplexer_1_out, multiplexer_2_out,
       multiplexer_3_out, multiplexer_4_out;

  and and_1 (and_1_out, WE, en);
  Demultiplexer #(.Selector_Bits(2)) demultiplexer_1 (
    .sel(A[1:0]), .in(and_1_out), .out_0(demultiplexer_1_out_0), .out_1(demultiplexer_1_out_1),
    .out_2(demultiplexer_1_out_2), .out_3(demultiplexer_1_out_3));
  Multiplexer #(.Bits(32)) multiplexer_1 (.sel(demultiplexer_1_out_0), .in_0(_1P), .in_1(Din), .out(multiplexer_1_out));
  Multiplexer #(.Bits(32)) multiplexer_2 (.sel(demultiplexer_1_out_1), .in_0(_2P), .in_1(Din), .out(multiplexer_2_out));
  Multiplexer #(.Bits(32)) multiplexer_3 (.sel(demultiplexer_1_out_2), .in_0(_3P), .in_1(Din), .out(multiplexer_3_out));
  Multiplexer #(.Bits(32)) multiplexer_4 (.sel(demultiplexer_1_out_3), .in_0(_4P), .in_1(Din), .out(multiplexer_4_out));
  D_FF #(.Bits(32)) d_ff_1 (.D(multiplexer_1_out), .C(C), .Q(d_ff_1_q));  // open: nQ
  D_FF #(.Bits(32)) d_ff_2 (.D(multiplexer_2_out), .C(C), .Q(d_ff_2_q));  // open: nQ
  D_FF #(.Bits(32)) d_ff_3 (.D(multiplexer_3_out), .C(C), .Q(d_ff_3_q));  // open: nQ
  D_FF #(.Bits(32)) d_ff_4 (.D(multiplexer_4_out), .C(C), .Q(d_ff_4_q));  // open: nQ
  Multiplexer #(.Selector_Bits(2), .Bits(32)) multiplexer_5 (
    .sel(A[1:0]), .in_0(d_ff_1_q), .in_1(d_ff_2_q), .in_2(d_ff_3_q), .in_3(d_ff_4_q), .out(D));
endmodule
