// Digital circuit MergeData.dig as structural Verilog
module MergeData (
  input  [31:0] D,
  input  [2:0] funct3,
  output [31:0] RD
);

  wire [31:0] bitextender_1_out, bitextender_2_out;

  BitExtender #(.outputBits(32)) bitextender_1 (.in(D[7:0]), .out(bitextender_1_out));
  BitExtender #(.inputBits(16), .outputBits(32)) bitextender_2 (.in(D[15:0]), .out(bitextender_2_out));
  Multiplexer #(.Selector_Bits(3), .Bits(32)) multiplexer_1 (
    .sel(funct3), .in_0(bitextender_1_out), .in_1(bitextender_2_out), .in_2(D), .in_3({32{1'b0}}),
    .in_4({{24{1'b0}}, D[7:0]}), .in_5({{16{1'b0}}, D[15:0]}), .in_6({32{1'b0}}), .in_7({32{1'b0}}), .out(RD));
endmodule
