// Digital circuit RAMViewer.dig as structural Verilog
module RAMViewer (
  input  CC,
  input  [31:0] _2D,
  output [23:0] _2A
);

  Counter #(.Bits(6)) counter_1 (.en(1'b1), .C(CC), .clr(1'b0), .out(_2A[7:2]));  // open: ovf
  LedMatrix #(.ledPersistence("true"), .colAddrBits(6), .rowDataBits(32)) ledmatrix_1 (.rows(_2D), .column(_2A[7:2]));

  assign {_2A[23:8], _2A[1:0]} = {18{1'b0}};

  // Notes on the sheet:
  //   CC: Hz: 5
endmodule
